// Logisim project exerc-1.circ as structural Verilog: 8 circuits, main circuit main
module main (
  input  A,
  input  B,
  input  C,
  input  D
);

  wire a_1_a_2, b_1_b_2, c_1_c_2, d_1_d_2, e_1_e, f_1_f, g_1_g;

  a a_1 (.D(A), .C(B), .B(C), .A(D), .a_2(a_1_a_2));
  b b_1 (.D(A), .C(B), .B(C), .A(D), .b_2(b_1_b_2));
  c c_1 (.D(A), .C(B), .B(C), .A(D), .c_2(c_1_c_2));
  d d_1 (.D(A), .C(B), .B(C), .A(D), .d_2(d_1_d_2));
  e e_1 (.D(A), .C(B), .B(C), .A(D), .e(e_1_e));
  f f_1 (.D(A), .C(B), .B(C), .A(D), .f(f_1_f));
  g g_1 (.D(A), .C(B), .B(C), .A(D), .g(g_1_g));
  _7_Segment_Display u_7_segment_display_1 (
    .g(g_1_g), .f(f_1_f), .a(a_1_a_2), .b(b_1_b_2), .e(e_1_e), .d(d_1_d_2), .c(c_1_c_2));  // open: dp
endmodule

module a (
  input  D,
  input  C,
  input  B,
  input  A,
  output a_2
);

  wire and_1_out, and_2_out, and_3_out, and_4_out, and_5_out, and_6_out, not_1_out, not_2_out, not_3_out,
       not_4_out, not_5_out, not_6_out, not_7_out;

  not not_1 (not_1_out, C);
  and and_1 (and_1_out, not_1_out, not_2_out);
  not not_2 (not_2_out, A);
  not not_3 (not_3_out, D);
  and and_2 (and_2_out, not_3_out, B);
  not not_4 (not_4_out, D);
  and and_3 (and_3_out, not_4_out, C, A);
  and and_4 (and_4_out, C, B);
  and and_5 (and_5_out, D, not_5_out, not_6_out);
  not not_5 (not_5_out, C);
  not not_6 (not_6_out, B);
  and and_6 (and_6_out, D, not_7_out);
  not not_7 (not_7_out, A);
  or or_1 (a_2, and_1_out, and_2_out, and_3_out, and_4_out, and_5_out, and_6_out);
endmodule

module b (
  input  D,
  input  C,
  input  B,
  input  A,
  output b_2
);

  wire and_1_out, and_2_out, and_3_out, and_4_out, and_5_out, and_6_out, not_1_out, not_2_out, not_3_out,
       not_4_out, not_5_out, not_6_out, not_7_out, not_8_out, not_9_out, not_10_out, not_11_out;

  not not_1 (not_1_out, D);
  and and_1 (and_1_out, not_1_out, not_2_out);
  not not_2 (not_2_out, C);
  not not_3 (not_3_out, D);
  and and_2 (and_2_out, not_3_out, not_4_out, not_5_out);
  not not_4 (not_4_out, B);
  not not_5 (not_5_out, A);
  not not_6 (not_6_out, C);
  and and_3 (and_3_out, not_6_out, not_7_out);
  not not_7 (not_7_out, B);
  not not_8 (not_8_out, C);
  and and_4 (and_4_out, not_8_out, not_9_out);
  not not_9 (not_9_out, A);
  not not_10 (not_10_out, D);
  and and_5 (and_5_out, not_10_out, B, A);
  and and_6 (and_6_out, D, not_11_out, A);
  not not_11 (not_11_out, B);
  or or_1 (b_2, and_1_out, and_2_out, and_3_out, and_4_out, and_5_out, and_6_out);
endmodule

module c (
  input  D,
  input  C,
  input  B,
  input  A,
  output c_2
);

  wire and_1_out, and_2_out, and_3_out, and_4_out, and_5_out, not_1_out, not_2_out, not_3_out, not_4_out,
       not_5_out, not_6_out;

  not not_1 (not_1_out, D);
  and and_1 (and_1_out, not_1_out, not_2_out);
  not not_2 (not_2_out, B);
  not not_3 (not_3_out, D);
  and and_2 (and_2_out, not_3_out, A);
  not not_4 (not_4_out, B);
  and and_3 (and_3_out, not_4_out, A);
  not not_5 (not_5_out, D);
  and and_4 (and_4_out, not_5_out, C);
  and and_5 (and_5_out, D, not_6_out);
  not not_6 (not_6_out, C);
  or or_1 (c_2, and_1_out, and_2_out, and_3_out, and_4_out, and_5_out);
endmodule

module d (
  input  D,
  input  C,
  input  B,
  input  A,
  output d_2
);

  wire and_1_out, and_2_out, and_3_out, and_4_out, and_5_out, not_1_out, not_2_out, not_3_out, not_4_out,
       not_5_out, not_6_out, not_7_out;

  not not_1 (not_1_out, D);
  and and_1 (and_1_out, not_1_out, not_2_out, not_3_out);
  not not_2 (not_2_out, C);
  not not_3 (not_3_out, A);
  not not_4 (not_4_out, C);
  and and_2 (and_2_out, not_4_out, B, A);
  and and_3 (and_3_out, C, not_5_out, A);
  not not_5 (not_5_out, B);
  and and_4 (and_4_out, C, B, not_6_out);
  not not_6 (not_6_out, A);
  and and_5 (and_5_out, D, not_7_out);
  not not_7 (not_7_out, B);
  or or_1 (d_2, and_1_out, and_2_out, and_3_out, and_4_out, and_5_out);
endmodule

module e (
  input  D,
  input  C,
  input  B,
  input  A,
  output e
);

  wire and_1_out, and_2_out, and_3_out, and_4_out, not_1_out, not_2_out, not_3_out;

  not not_1 (not_1_out, C);
  and and_1 (and_1_out, not_1_out, not_2_out);
  not not_2 (not_2_out, A);
  and and_2 (and_2_out, B, not_3_out);
  not not_3 (not_3_out, A);
  and and_3 (and_3_out, D, B);
  and and_4 (and_4_out, D, C);
  or or_1 (e, and_1_out, and_2_out, and_3_out, and_4_out);
endmodule

module f (
  input  D,
  input  C,
  input  B,
  input  A,
  output f
);

  wire and_1_out, and_2_out, and_3_out, and_4_out, and_5_out, not_1_out, not_2_out, not_3_out, not_4_out,
       not_5_out, not_6_out;

  not not_1 (not_1_out, B);
  and and_1 (and_1_out, not_1_out, not_2_out);
  not not_2 (not_2_out, A);
  not not_3 (not_3_out, D);
  and and_2 (and_2_out, not_3_out, C, not_4_out);
  not not_4 (not_4_out, B);
  and and_3 (and_3_out, C, not_5_out);
  not not_5 (not_5_out, A);
  and and_4 (and_4_out, D, not_6_out);
  not not_6 (not_6_out, C);
  and and_5 (and_5_out, D, B);
  or or_1 (f, and_1_out, and_2_out, and_3_out, and_4_out, and_5_out);
endmodule

module g (
  input  D,
  input  C,
  input  B,
  input  A,
  output g
);

  wire and_1_out, and_2_out, and_3_out, and_4_out, and_5_out, not_1_out, not_2_out, not_3_out, not_4_out,
       not_5_out;

  not not_1 (not_1_out, C);
  and and_1 (and_1_out, not_1_out, B);
  and and_2 (and_2_out, B, not_2_out);
  not not_2 (not_2_out, A);
  not not_3 (not_3_out, D);
  and and_3 (and_3_out, not_3_out, C, not_4_out);
  not not_4 (not_4_out, B);
  and and_4 (and_4_out, D, not_5_out);
  not not_5 (not_5_out, C);
  and and_5 (and_5_out, D, A);
  or or_1 (g, and_1_out, and_2_out, and_3_out, and_4_out, and_5_out);
endmodule
