// Logisim project exerc-2.circ as structural Verilog
module ula (
);

  // AND_Gate and_1 is placed but not wired
  // OR_Gate or_1 is placed but not wired
  // NAND_Gate nand_1 is placed but not wired
  // XOR_Gate xor_1 is placed but not wired
endmodule

module full_adder (
  input  A,
  input  B,
  input  carry_in,
  output sum,
  output carry_out
);

  wire half_adder_1_carry, half_adder_1_sum, half_adder_2_carry;

  half_adder half_adder_1 (.A(A), .B(B), .sum(half_adder_1_sum), .carry(half_adder_1_carry));
  half_adder half_adder_2 (.A(half_adder_1_sum), .B(carry_in), .sum(sum), .carry(half_adder_2_carry));
  or or_1 (carry_out, half_adder_2_carry, half_adder_1_carry);
endmodule

module half_adder (
  input  A,
  input  B,
  output sum,
  output carry
);

  xor xor_1 (sum, A, B);
  and and_1 (carry, A, B);
endmodule

module full_subtractor (
  input  A,
  input  B,
  input  in_3,
  output out_4,
  output out_5
);

  wire and_1_out, and_2_out, and_3_out, not_1_out, or_1_out, xor_1_out;

  not not_1 (not_1_out, A);
  and and_1 (and_1_out, not_1_out, B);
  and and_2 (and_2_out, not_1_out, in_3);
  xor xor_1 (xor_1_out, A, B);
  or or_1 (or_1_out, and_1_out, and_2_out);
  xor xor_2 (out_4, xor_1_out, in_3);
  and and_3 (and_3_out, in_3, B);
  or or_2 (out_5, or_1_out, and_3_out);
endmodule
