// Logisim project exerc-2.circ as structural Verilog: 6 circuits, main circuit main
module main (
  input  in_1,
  input  in_2,
  output out_3,
  output out_4
);

  full_adder full_adder_1 (.A(in_1), .B(in_2), .sum(out_3), .carry_out(out_4));  // open: carry_in
endmodule

module ula (
  input  [7:0] in_1,
  input  [1:0] in_2,
  output [7:0] out_3,
  output out_4
);

  wire [7:0] n8_bits_adder_1_p1;

  // _8_bits_adder 8_bits_adder_1: pin names not known; wires that end beside it: n8_bits_adder_1_p1, n8_bits_adder_1_p1, n8_bits_adder_1_p1, n8_bits_adder_1_p1, n8_bits_adder_1_p1, n8_bits_adder_1_p1, n8_bits_adder_1_p1, n8_bits_adder_1_p1
  Multiplexer #(.select(2), .width(8)) multiplexer_1 (
    .in0(n8_bits_adder_1_p1), .out(out_3), .sel(in_2), .en(out_4));  // open: in1, in2, in3
endmodule

module full_adder (
  input  A,
  input  B,
  input  carry_in,
  output sum,
  output carry_out
);

  wire half_adder_1_carry, half_adder_1_sum, half_adder_2_carry;

  half_adder half_adder_1 (.A(A), .B(B), .sum(half_adder_1_sum), .carry(half_adder_1_carry));
  half_adder half_adder_2 (.A(half_adder_1_sum), .B(carry_in), .sum(sum), .carry(half_adder_2_carry));
  or or_1 (carry_out, half_adder_2_carry, half_adder_1_carry);
endmodule

module half_adder (
  input  A,
  input  B,
  output sum,
  output carry
);

  xor xor_1 (sum, A, B);
  and and_1 (carry, A, B);
endmodule

module _8_bits_adder (
  input  in_1,
  input  in_2,
  input  in_3,
  input  in_4,
  input  in_5,
  input  in_6,
  input  in_7,
  input  in_8,
  input  in_9,
  input  in_10,
  input  in_11,
  input  in_12,
  input  in_13,
  input  in_14,
  input  in_15,
  input  in_16,
  output out_17,
  output out_18,
  output out_19,
  output out_20,
  output out_21,
  output out_22,
  output out_23,
  output out_24,
  output out_25
);

  wire full_adder_2_carry_out, full_adder_3_carry_out, full_adder_4_carry_out, full_adder_5_carry_out,
       full_adder_6_carry_out, full_adder_7_carry_out, half_adder_1_carry;

  full_adder full_adder_1 (.A(in_1), .B(in_2), .carry_in(full_adder_2_carry_out), .sum(out_17), .carry_out(out_25));
  full_adder full_adder_2 (
    .A(in_3), .B(in_4), .carry_in(full_adder_3_carry_out), .sum(out_18), .carry_out(full_adder_2_carry_out));
  full_adder full_adder_3 (
    .A(in_5), .B(in_6), .carry_in(full_adder_4_carry_out), .sum(out_19), .carry_out(full_adder_3_carry_out));
  full_adder full_adder_4 (
    .A(in_7), .B(in_8), .carry_in(full_adder_5_carry_out), .sum(out_20), .carry_out(full_adder_4_carry_out));
  full_adder full_adder_5 (
    .A(in_9), .B(in_10), .carry_in(full_adder_6_carry_out), .sum(out_21), .carry_out(full_adder_5_carry_out));
  full_adder full_adder_6 (
    .A(in_11), .B(in_12), .carry_in(full_adder_7_carry_out), .sum(out_22), .carry_out(full_adder_6_carry_out));
  full_adder full_adder_7 (
    .A(in_13), .B(in_14), .carry_in(half_adder_1_carry), .sum(out_23), .carry_out(full_adder_7_carry_out));
  half_adder half_adder_1 (.A(in_15), .B(in_16), .sum(out_24), .carry(half_adder_1_carry));
endmodule

module full_subtractor (
  input  A,
  input  B,
  input  in_3,
  output out_4,
  output out_5
);

  wire and_1_out, and_2_out, and_3_out, not_1_out, or_1_out, xor_1_out;

  not not_1 (not_1_out, A);
  and and_1 (and_1_out, not_1_out, B);
  and and_2 (and_2_out, not_1_out, in_3);
  xor xor_1 (xor_1_out, A, B);
  or or_1 (or_1_out, and_1_out, and_2_out);
  xor xor_2 (out_4, xor_1_out, in_3);
  and and_3 (and_3_out, in_3, B);
  or or_2 (out_5, or_1_out, and_3_out);
endmodule
