// Logisim project atv02.circ as structural Verilog
module \Registrador_Síncrono  (
  input  X0,
  input  X1,
  input  X2,
  input  X3,
  input  [1:0] CTRL,
  output Y0,
  output Y1,
  output Y2,
  output Y3
);

  wire CK_out, multiplexer_1_out, multiplexer_2_out, multiplexer_3_out, multiplexer_4_out, not_1_out,
       not_2_out, not_3_out, not_4_out;

  Clock CK (.out(CK_out));
  not not_1 (not_1_out, Y0);
  D_Flip_Flop d_ff_1 (.clk(CK_out), .D(multiplexer_1_out), .Q(Y0));  // open: Qn, preset, en, reset
  Multiplexer #(.select(2)) multiplexer_1 (
    .in0(Y0), .in1(X0), .in2(not_1_out), .in3(Y2), .out(multiplexer_1_out), .sel(CTRL));  // open: en
  not not_2 (not_2_out, Y1);
  Multiplexer #(.select(2)) multiplexer_2 (
    .in0(Y1), .in1(X1), .in2(not_2_out), .in3(Y3), .out(multiplexer_2_out), .sel(CTRL));  // open: en
  D_Flip_Flop d_ff_2 (.clk(CK_out), .D(multiplexer_2_out), .Q(Y1));  // open: Qn, preset, en, reset
  not not_3 (not_3_out, Y2);
  Multiplexer #(.select(2)) multiplexer_3 (
    .in0(Y2), .in1(X2), .in2(not_3_out), .in3(Y0), .out(multiplexer_3_out), .sel(CTRL));  // open: en
  D_Flip_Flop d_ff_3 (.clk(CK_out), .D(multiplexer_3_out), .Q(Y2));  // open: Qn, preset, en, reset
  not not_4 (not_4_out, Y3);
  Multiplexer #(.select(2)) multiplexer_4 (
    .in0(Y3), .in1(X3), .in2(not_4_out), .in3(Y1), .out(multiplexer_4_out), .sel(CTRL));  // open: en
  D_Flip_Flop d_ff_4 (.clk(CK_out), .D(multiplexer_4_out), .Q(Y3));  // open: Qn, preset, en, reset
endmodule
