// Logisim project atv03.circ as structural Verilog: 2 circuits, main circuit main
module main (
  input  [3:0] in_1,
  input  in_2,
  input  [1:0] in_3,
  output [3:0] out_4
);

  \Registrador_Síncrono  \registrador_síncrono_1  (
    .X0(in_1[0]), .X1(in_1[1]), .X2(in_1[2]), .X3(in_1[3]), .CLK(in_2), .CTRL(in_3), .Y0(out_4[0]),
    .Y1(out_4[1]), .Y2(out_4[2]), .Y3(out_4[3]));
endmodule

module \Registrador_Síncrono  (
  input  X0,
  input  X1,
  input  X2,
  input  X3,
  input  CLK,
  input  [1:0] CTRL,
  output Y0,
  output Y1,
  output Y2,
  output Y3
);

  wire multiplexer_1_out, multiplexer_2_out, multiplexer_3_out, multiplexer_4_out, not_1_out, not_2_out,
       not_3_out, not_4_out;

  not not_1 (not_1_out, Y0);
  D_Flip_Flop d_ff_1 (.clk(CLK), .D(multiplexer_1_out), .Q(Y0));  // open: Qn, preset, en, reset
  Multiplexer #(.select(2)) multiplexer_1 (
    .in0(Y0), .in1(X0), .in2(not_1_out), .in3(Y2), .out(multiplexer_1_out), .sel(CTRL));  // open: en
  Multiplexer #(.select(2)) multiplexer_2 (
    .in0(Y1), .in1(X1), .in2(not_2_out), .in3(Y3), .out(multiplexer_2_out), .sel(CTRL));  // open: en
  not not_2 (not_2_out, Y1);
  D_Flip_Flop d_ff_2 (.clk(CLK), .D(multiplexer_2_out), .Q(Y1));  // open: Qn, preset, en, reset
  not not_3 (not_3_out, Y2);
  Multiplexer #(.select(2)) multiplexer_3 (
    .in0(Y2), .in1(X2), .in2(not_3_out), .in3(Y0), .out(multiplexer_3_out), .sel(CTRL));  // open: en
  D_Flip_Flop d_ff_3 (.clk(CLK), .D(multiplexer_3_out), .Q(Y2));  // open: Qn, preset, en, reset
  Multiplexer #(.select(2)) multiplexer_4 (
    .in0(Y3), .in1(X3), .in2(not_4_out), .in3(Y1), .out(multiplexer_4_out), .sel(CTRL));  // open: en
  not not_4 (not_4_out, Y3);
  D_Flip_Flop d_ff_4 (.clk(CLK), .D(multiplexer_4_out), .Q(Y3));  // open: Qn, preset, en, reset
endmodule
