// Logisim project exerc-3.circ as structural Verilog: 2 circuits, main circuit main
module main (
  input  [7:0] in_1,
  input  shift_in,
  input  [1:0] CTR,
  output [7:0] out_4
);

  wire clock_1_out;

  Clock clock_1 (.out(clock_1_out));
  Registrador_sincrono registrador_sincrono_1 (
    .x1(in_1[0]), .x2(in_1[1]), .x3(in_1[2]), .x4(in_1[3]), .x5(in_1[4]), .x6(in_1[5]), .x7(in_1[6]),
    .x8(in_1[7]), .shift_in(shift_in), .CLK(clock_1_out), .CTL(CTR), .y1(out_4[0]), .y2(out_4[1]),
    .y3(out_4[2]), .y4(out_4[3]), .y5(out_4[4]), .y6(out_4[5]), .y7(out_4[6]), .y8(out_4[7]));
endmodule

module Registrador_sincrono (
  input  x1,
  input  x2,
  input  x3,
  input  x4,
  input  x5,
  input  x6,
  input  x7,
  input  x8,
  input  shift_in,
  input  CLK,
  input  [1:0] CTL,
  output y1,
  output y2,
  output y3,
  output y4,
  output y5,
  output y6,
  output y7,
  output y8
);

  wire multiplexer_1_out, multiplexer_2_out, multiplexer_3_out, multiplexer_4_out, multiplexer_5_out,
       multiplexer_6_out, multiplexer_7_out, multiplexer_8_out;

  Multiplexer #(.select(2)) multiplexer_1 (
    .in0(y1), .in1(x1), .in2(y2), .in3(y2), .out(multiplexer_1_out), .sel(CTL));  // open: en
  Multiplexer #(.select(2)) multiplexer_2 (
    .in0(y5), .in1(x5), .in2(y6), .in3(y6), .out(multiplexer_2_out), .sel(CTL));  // open: en
  D_Flip_Flop d_ff_1 (.clk(CLK), .D(multiplexer_1_out), .Q(y1));  // open: Qn, preset, en, reset
  D_Flip_Flop d_ff_2 (.clk(CLK), .D(multiplexer_2_out), .Q(y5));  // open: Qn, preset, en, reset
  Multiplexer #(.select(2)) multiplexer_3 (
    .in0(y2), .in1(x2), .in2(y3), .in3(y3), .out(multiplexer_3_out), .sel(CTL));  // open: en
  Multiplexer #(.select(2)) multiplexer_4 (
    .in0(y6), .in1(x6), .in2(y7), .in3(y7), .out(multiplexer_4_out), .sel(CTL));  // open: en
  D_Flip_Flop d_ff_3 (.clk(CLK), .D(multiplexer_3_out), .Q(y2));  // open: Qn, preset, en, reset
  D_Flip_Flop d_ff_4 (.clk(CLK), .D(multiplexer_4_out), .Q(y6));  // open: Qn, preset, en, reset
  D_Flip_Flop d_ff_5 (.clk(CLK), .D(multiplexer_5_out), .Q(y3));  // open: Qn, preset, en, reset
  Multiplexer #(.select(2)) multiplexer_5 (
    .in0(y3), .in1(x3), .in2(y4), .in3(y4), .out(multiplexer_5_out), .sel(CTL));  // open: en
  D_Flip_Flop d_ff_6 (.clk(CLK), .D(multiplexer_6_out), .Q(y7));  // open: Qn, preset, en, reset
  Multiplexer #(.select(2)) multiplexer_6 (
    .in0(y7), .in1(x7), .in2(y8), .in3(y8), .out(multiplexer_6_out), .sel(CTL));  // open: en
  Multiplexer #(.select(2)) multiplexer_7 (
    .in0(y4), .in1(x4), .in2(y5), .in3(y5), .out(multiplexer_7_out), .sel(CTL));  // open: en
  Multiplexer #(.select(2)) multiplexer_8 (
    .in0(y8), .in1(x8), .in2(shift_in), .out(multiplexer_8_out), .sel(CTL));  // open: in3, en
  D_Flip_Flop d_ff_7 (.clk(CLK), .D(multiplexer_7_out), .Q(y4));  // open: Qn, preset, en, reset
  D_Flip_Flop d_ff_8 (.clk(CLK), .D(multiplexer_8_out), .Q(y8));  // open: Qn, preset, en, reset
endmodule
