// Logisim project circuito_bugado.circ as structural Verilog: 9 circuits, main circuit N2_B'
module N2_B (
  input  A,
  input  S2,
  input  S1,
  input  S0,
  output N2
);

  wire and_1_out, and_2_out, and_3_out, not_1_out, not_2_out, not_3_out;

  not not_1 (not_1_out, S1);
  and and_1 (and_1_out, S2, not_1_out, not_2_out);
  not not_2 (not_2_out, S0);
  and and_2 (and_2_out, S2, S1, S0);
  not not_3 (not_3_out, S2);
  and and_3 (and_3_out, A, not_3_out, S1);
  or or_1 (N2, and_1_out, and_2_out, and_3_out);
endmodule

module N2_B_2 (
  input  A,
  input  S2,
  input  S1,
  input  S0,
  output N2
);

  wire and_1_out, and_2_out, and_3_out, and_4_out, not_1_out, not_2_out, not_3_out, not_4_out;

  and and_1 (and_1_out, S1, S0);
  not not_1 (not_1_out, S1);
  and and_2 (and_2_out, S2, not_1_out, not_2_out);
  not not_2 (not_2_out, S0);
  not not_3 (not_3_out, S2);
  and and_3 (and_3_out, A, not_3_out, S0);
  and and_4 (and_4_out, A, not_4_out, S1);
  not not_4 (not_4_out, S2);
  or or_1 (N2, and_1_out, and_2_out, and_3_out, and_4_out);
endmodule

module N1_B (
  input  A,
  input  S2,
  input  S1,
  input  S0,
  output N1
);

  wire and_1_out, and_2_out, and_3_out, and_4_out, not_1_out, not_2_out, not_3_out, not_4_out, not_5_out,
       not_6_out;

  not not_1 (not_1_out, A);
  not not_2 (not_2_out, S2);
  and and_1 (and_1_out, not_1_out, not_2_out, S1);
  and and_2 (and_2_out, S2, S1, S0);
  not not_3 (not_3_out, S2);
  and and_3 (and_3_out, A, not_3_out, not_4_out);
  not not_4 (not_4_out, S1);
  not not_5 (not_5_out, S1);
  and and_4 (and_4_out, A, not_5_out, not_6_out);
  not not_6 (not_6_out, S0);
  or or_1 (N1, and_1_out, and_2_out, and_3_out, and_4_out);
endmodule

module N1_B_2 (
  input  A,
  input  S2,
  input  S1,
  input  S0,
  output N1
);

  wire and_1_out, and_2_out, and_3_out, and_4_out, not_1_out, not_2_out, not_3_out, not_4_out, not_5_out;

  not not_1 (not_1_out, A);
  not not_2 (not_2_out, S2);
  not not_3 (not_3_out, S0);
  not not_4 (not_4_out, S1);
  not not_5 (not_5_out, S0);
  and and_1 (and_1_out, not_1_out, not_2_out, S1, not_3_out);
  and and_2 (and_2_out, S2, S1, S0);
  and and_3 (and_3_out, A, not_4_out, not_5_out);
  and and_4 (and_4_out, A, S1, S0);
  or or_1 (N1, and_1_out, and_2_out, and_3_out, and_4_out);
endmodule

module N0_B (
  input  A,
  input  S2,
  input  S1,
  input  S0,
  output N0
);

  wire not_1_out;

  not not_1 (not_1_out, S2);
  and and_1 (N0, not_1_out, S0);
endmodule

module N0_B_2 (
  input  A,
  input  S2,
  input  S1,
  input  S0,
  output N0
);

  wire and_1_out, and_2_out, not_1_out, not_2_out, not_3_out, not_4_out;

  not not_1 (not_1_out, S2);
  and and_1 (and_1_out, not_1_out, not_2_out);
  not not_2 (not_2_out, S0);
  not not_3 (not_3_out, S1);
  and and_2 (and_2_out, not_3_out, not_4_out);
  not not_4 (not_4_out, S0);
  or or_1 (N0, and_1_out, and_2_out);
endmodule

module R (
  input  A,
  input  S1,
  input  S0,
  output R
);

  wire and_1_out, and_2_out, not_1_out, not_2_out;

  not not_1 (not_1_out, S1);
  not not_2 (not_2_out, S0);
  and and_1 (and_1_out, A, not_1_out, S0);
  and and_2 (and_2_out, A, S1, not_2_out);
  or or_1 (R, and_1_out, and_2_out);
endmodule

module T (
  input  A,
  input  S1,
  input  S0,
  output T
);

  and and_1 (T, A, S1);
endmodule

module main (
  input  A,
  input  B
);

  wire clock_1_out;

  N0_B_2 n0_b_1 ();  // open: A, S2, S1, S0, N0
  N0_B n0_b_2 ();  // open: A, S2, S1, S0, N0
  N1_B_2 n1_b_1 ();  // open: A, S2, S1, S0, N1
  N1_B n1_b_2 ();  // open: A, S2, S1, S0, N1
  N2_B_2 n2_b_1 ();  // open: A, S2, S1, S0, N2
  N2_B n2_b_2 ();  // open: A, S2, S1, S0, N2
  Clock clock_1 (.out(clock_1_out));
  D_Flip_Flop d_ff_1 (.clk(clock_1_out));  // open: D, Q, Qn, preset, en, reset
  D_Flip_Flop d_ff_2 (.clk(clock_1_out));  // open: D, Q, Qn, preset, en, reset
  D_Flip_Flop d_ff_3 (.clk(clock_1_out));  // open: D, Q, Qn, preset, en, reset
endmodule
