// Logisim project exerc-4.circ as structural Verilog: 6 circuits, main circuit R
module R (
  input  S2,
  input  S1,
  input  S0,
  output R
);

  wire and_1_out, and_2_out, not_1_out, not_2_out;

  not not_1 (not_1_out, S1);
  not not_2 (not_2_out, S0);
  and and_1 (and_1_out, S2, not_1_out, S0);
  and and_2 (and_2_out, S2, S1, not_2_out);
  or or_1 (R, and_1_out, and_2_out);
endmodule

module T (
  input  S2,
  input  S1,
  input  S0,
  output T
);

  and and_1 (T, S2, S1);
endmodule

module N0 (
  input  B,
  input  A,
  input  S2,
  input  S1,
  input  S0,
  output N0
);

  wire and_1_out, and_2_out, and_3_out, not_1_out, not_2_out, not_3_out, not_4_out, not_5_out, not_6_out;

  not not_1 (not_1_out, B);
  not not_2 (not_2_out, S2);
  not not_3 (not_3_out, S2);
  not not_4 (not_4_out, S0);
  not not_5 (not_5_out, S1);
  not not_6 (not_6_out, S0);
  and and_1 (and_1_out, not_1_out, not_2_out, S0);
  and and_2 (and_2_out, B, not_3_out, not_4_out);
  and and_3 (and_3_out, B, not_5_out, not_6_out);
  or or_1 (N0, and_1_out, and_2_out, and_3_out);
endmodule

module N1 (
  input  B,
  input  A,
  input  S2,
  input  S1,
  input  S0,
  output N1
);

  wire and_1_out, and_2_out, and_3_out, and_4_out, and_5_out, and_6_out, and_7_out, not_1_out, not_2_out,
       not_3_out, not_4_out, not_5_out, not_6_out, not_7_out, not_8_out, not_9_out, not_10_out, not_11_out,
       not_12_out, not_13_out, not_14_out;

  not not_1 (not_1_out, B);
  not not_2 (not_2_out, A);
  not not_3 (not_3_out, S2);
  not not_4 (not_4_out, A);
  not not_5 (not_5_out, S2);
  not not_6 (not_6_out, S0);
  not not_7 (not_7_out, B);
  not not_8 (not_8_out, S2);
  not not_9 (not_9_out, S1);
  not not_10 (not_10_out, S1);
  not not_11 (not_11_out, S0);
  not not_12 (not_12_out, A);
  not not_13 (not_13_out, S2);
  not not_14 (not_14_out, S1);
  and and_1 (and_1_out, not_1_out, not_2_out, not_3_out, S1);
  and and_2 (and_2_out, not_4_out, not_5_out, S1, not_6_out);
  and and_3 (and_3_out, S2, S1, S0);
  and and_4 (and_4_out, not_7_out, A, not_8_out, not_9_out);
  and and_5 (and_5_out, A, not_10_out, not_11_out);
  and and_6 (and_6_out, B, not_12_out, not_13_out, not_14_out, S0);
  and and_7 (and_7_out, B, A, S1, S0);
  or or_1 (N1, and_1_out, and_2_out, and_3_out, and_4_out, and_5_out, and_6_out, and_7_out);
endmodule

module N2 (
  input  B,
  input  A,
  input  S2,
  input  S1,
  input  S0,
  output N2
);

  wire and_1_out, and_2_out, and_3_out, and_4_out, and_5_out, not_1_out, not_2_out, not_3_out, not_4_out;

  not not_1 (not_1_out, S1);
  not not_2 (not_2_out, S0);
  not not_3 (not_3_out, S2);
  not not_4 (not_4_out, S2);
  and and_1 (and_1_out, S2, not_1_out, not_2_out);
  and and_2 (and_2_out, S2, S1, S0);
  and and_3 (and_3_out, A, not_3_out, S1);
  and and_4 (and_4_out, B, S1, S0);
  and and_5 (and_5_out, B, A, not_4_out, S0);
  or or_1 (N2, and_1_out, and_2_out, and_3_out, and_4_out, and_5_out);
endmodule

module main (
  input  A,
  input  B,
  output out_3,
  output out_4
);

  wire clock_1_out, n0_1_n0, n1_1_n1, n2_1_n2, S0_q, S1_q, S2_q;

  Clock clock_1 (.out(clock_1_out));
  N0 n0_1 (.B(B), .A(A), .S2(S2_q), .S1(S1_q), .S0(S0_q), .N0(n0_1_n0));
  N1 n1_1 (.B(B), .A(A), .S2(S2_q), .S1(S1_q), .S0(S0_q), .N1(n1_1_n1));
  N2 n2_1 (.B(B), .A(A), .S2(S2_q), .S1(S1_q), .S0(S0_q), .N2(n2_1_n2));
  D_Flip_Flop S0 (.clk(clock_1_out), .D(n0_1_n0), .Q(S0_q));  // open: Qn, preset, en, reset
  D_Flip_Flop S1 (.clk(clock_1_out), .D(n1_1_n1), .Q(S1_q));  // open: Qn, preset, en, reset
  D_Flip_Flop S2 (.clk(clock_1_out), .D(n2_1_n2), .Q(S2_q));  // open: Qn, preset, en, reset
  R r_1 (.S2(S2_q), .S1(S1_q), .S0(S0_q), .R(out_3));
  T t_1 (.S2(S2_q), .S1(S1_q), .S0(S0_q), .T(out_4));
endmodule
