// Logisim project aula02_turmaB.circ as structural Verilog: 10 circuits, main circuit main
module main (
  input  in_1,
  input  in_2,
  input  in_3,
  input  in_4,
  output out_5,
  output out_6
);

  FlipFlop flipflop_1 (.D(in_1), .CLK(in_2), .out_3(out_5));  // open: out_4
  D_Flip_Flop d_ff_1 (.clk(in_3), .D(in_4), .Q(out_6));  // open: Qn, preset, en, reset
endmodule

module mux2 (
  input  A,
  input  B,
  input  sel,
  output out
);

  wire and_1_out, and_2_out, not_1_out;

  not not_1 (not_1_out, sel);
  and and_1 (and_1_out, A, not_1_out);
  and and_2 (and_2_out, sel, B);
  or or_1 (out, and_1_out, and_2_out);
endmodule

module mux4 (
  input  A,
  input  B,
  input  C,
  input  D,
  input  sel0,
  input  sel1,
  output out_7
);

  wire mux2_1_out, mux2_2_out;

  mux2 mux2_1 (.A(A), .B(B), .sel(sel0), .out(mux2_1_out));
  mux2 mux2_2 (.A(C), .B(D), .sel(sel0), .out(mux2_2_out));
  mux2 mux2_3 (.A(mux2_1_out), .B(mux2_2_out), .sel(sel1), .out(out_7));
endmodule

module half_adder (
  input  A,
  input  B,
  output Sum,
  output C_out
);

  xor xor_1 (Sum, A, B);
  and and_1 (C_out, A, B);
endmodule

module full_adder (
  input  A,
  input  B,
  input  C_in,
  output Sum,
  output C_out
);

  wire half_adder_1_c_out, half_adder_1_sum, half_adder_2_c_out;

  half_adder half_adder_1 (.A(A), .B(B), .Sum(half_adder_1_sum), .C_out(half_adder_1_c_out));
  half_adder half_adder_2 (.A(half_adder_1_sum), .B(C_in), .Sum(Sum), .C_out(half_adder_2_c_out));
  or or_1 (C_out, half_adder_2_c_out, half_adder_1_c_out);
endmodule

module _4_bits_adder (
  input  in_1,
  input  in_2,
  input  in_3,
  input  in_4,
  input  in_5,
  input  in_6,
  output out_7,
  output out_8,
  output out_9,
  output out_10
);

  wire full_adder_1_c_out, half_adder_1_c_out;

  half_adder half_adder_1 (.A(in_1), .B(in_4), .Sum(out_7), .C_out(half_adder_1_c_out));
  full_adder full_adder_1 (.A(in_2), .B(in_5), .C_in(half_adder_1_c_out), .Sum(out_8), .C_out(full_adder_1_c_out));
  full_adder full_adder_2 (.A(in_3), .B(in_6), .C_in(full_adder_1_c_out), .Sum(out_9), .C_out(out_10));
endmodule

module latch_RS (
  input  R,
  input  S,
  output Q,
  output nQ
);

  nor nor_1 (Q, R, nQ);
  nor nor_2 (nQ, Q, S);
endmodule

module latch_RS_c_enable (
  input  R,
  input  S,
  input  enable,
  output Q,
  output nQ
);

  wire and_1_out, and_2_out;

  and and_1 (and_1_out, R, enable);
  and and_2 (and_2_out, enable, S);
  nor nor_1 (Q, and_1_out, nQ);
  nor nor_2 (nQ, Q, and_2_out);
endmodule

module FlipFlop (
  input  D,
  input  CLK,
  output out_3,
  output out_4
);

  wire edge_detector_1_pos_edge, not_1_out;

  edge_detector edge_detector_1 (.CLK(CLK), .pos_edge(edge_detector_1_pos_edge));
  not not_1 (not_1_out, D);
  latch_RS_c_enable latch_rs_c_enable_1 (
    .R(not_1_out), .S(D), .enable(edge_detector_1_pos_edge), .Q(out_3), .nQ(out_4));
endmodule

module edge_detector (
  input  CLK,
  output pos_edge
);

  wire not_1_out, not_2_out, not_3_out;

  not not_1 (not_1_out, CLK);
  not not_2 (not_2_out, not_3_out);
  not not_3 (not_3_out, not_1_out);
  and and_1 (pos_edge, not_2_out, CLK);
endmodule
