// Logisim project aula03_B.circ as structural Verilog
module reg_in_par_out_par (
  input  in_1,
  input  in_2,
  input  in_3,
  input  in_4,
  input  in_5,
  output out_6,
  output out_7,
  output out_8,
  output out_9
);

  D_Flip_Flop d_ff_1 (.clk(in_5), .D(in_1), .Q(out_6));  // open: Qn, preset, en, reset
  D_Flip_Flop d_ff_2 (.clk(in_5), .D(in_2), .Q(out_7));  // open: Qn, preset, en, reset
  D_Flip_Flop d_ff_3 (.clk(in_5), .D(in_3), .Q(out_8));  // open: Qn, preset, en, reset
  D_Flip_Flop d_ff_4 (.clk(in_5), .D(in_4), .Q(out_9));  // open: Qn, preset, en, reset
endmodule

module reg_in_ser_out_ser (
  input  in_1,
  input  in_2,
  output out_3
);

  wire d_ff_1_q, d_ff_2_q, d_ff_3_q;

  D_Flip_Flop d_ff_1 (.clk(in_2), .D(in_1), .Q(d_ff_1_q));  // open: Qn, preset, en, reset
  D_Flip_Flop d_ff_2 (.clk(in_2), .D(d_ff_1_q), .Q(d_ff_2_q));  // open: Qn, preset, en, reset
  D_Flip_Flop d_ff_3 (.clk(in_2), .D(d_ff_2_q), .Q(d_ff_3_q));  // open: Qn, preset, en, reset
  D_Flip_Flop d_ff_4 (.clk(in_2), .D(d_ff_3_q), .Q(out_3));  // open: Qn, preset, en, reset
endmodule

module reg_in_ser_out_par (
  input  in_1,
  input  in_2,
  output out_3,
  output out_4,
  output out_5,
  output out_6
);

  D_Flip_Flop d_ff_1 (.clk(in_2), .D(in_1), .Q(out_6));  // open: Qn, preset, en, reset
  D_Flip_Flop d_ff_2 (.clk(in_2), .D(out_6), .Q(out_5));  // open: Qn, preset, en, reset
  D_Flip_Flop d_ff_3 (.clk(in_2), .D(out_5), .Q(out_4));  // open: Qn, preset, en, reset
  D_Flip_Flop d_ff_4 (.clk(in_2), .D(out_4), .Q(out_3));  // open: Qn, preset, en, reset
endmodule

module reg_in_par_out_ser (
  input  clk,
  input  b0,
  input  b1,
  input  b2,
  input  b3,
  input  shift_load,
  output out
);

  wire d_ff_1_q, d_ff_2_q, d_ff_3_q, multiplexer_1_out, multiplexer_2_out, multiplexer_3_out,
       multiplexer_4_out;

  Multiplexer #(.enable("false")) multiplexer_1 (.in0(b3), .in1(1'b0), .out(multiplexer_1_out), .sel(shift_load));
  D_Flip_Flop d_ff_1 (.clk(clk), .D(multiplexer_1_out), .Q(d_ff_1_q));  // open: Qn, preset, en, reset
  D_Flip_Flop d_ff_2 (.clk(clk), .D(multiplexer_2_out), .Q(d_ff_2_q));  // open: Qn, preset, en, reset
  Multiplexer #(.enable("false")) multiplexer_2 (.in0(b2), .in1(d_ff_1_q), .out(multiplexer_2_out), .sel(shift_load));
  D_Flip_Flop d_ff_3 (.clk(clk), .D(multiplexer_3_out), .Q(d_ff_3_q));  // open: Qn, preset, en, reset
  Multiplexer #(.enable("false")) multiplexer_3 (.in0(b1), .in1(d_ff_2_q), .out(multiplexer_3_out), .sel(shift_load));
  Multiplexer #(.enable("false")) multiplexer_4 (.in0(b0), .in1(d_ff_3_q), .out(multiplexer_4_out), .sel(shift_load));
  D_Flip_Flop d_ff_4 (.clk(clk), .D(multiplexer_4_out), .Q(out));  // open: Qn, preset, en, reset
endmodule

module state_machine_counter (
  input  x,
  output out_2,
  output out_3
);

  wire A_qn, and_1_out, and_2_out, and_3_out, clock_1_out, d_ff_1_qn, not_1_out, or_1_out, xor_1_out;

  Clock clock_1 (.out(clock_1_out));
  D_Flip_Flop A (.clk(clock_1_out), .D(or_1_out), .Q(out_3), .Qn(A_qn));  // open: preset, en, reset
  not not_1 (not_1_out, x);
  D_Flip_Flop d_ff_1 (.clk(clock_1_out), .D(xor_1_out), .Q(out_2), .Qn(d_ff_1_qn));  // open: preset, en, reset
  and and_1 (and_1_out, not_1_out, out_3);
  and and_2 (and_2_out, out_3, d_ff_1_qn);
  and and_3 (and_3_out, x, A_qn, out_2);
  or or_1 (or_1_out, and_1_out, and_2_out, and_3_out);
  xor xor_1 (xor_1_out, out_2, x);
endmodule
