// Logisim project teste.circ as structural Verilog: 1 circuit, main circuit main
module main (
  input  A,
  input  R,
  input  B,
  input  T
);

  wire clock_1_out, S1_2_qn, S1_qn, S2_qn;

  Clock clock_1 (.out(clock_1_out));
  D_Flip_Flop S2 (.clk(clock_1_out), .Qn(S2_qn));  // open: D, Q, preset, en, reset
  D_Flip_Flop S1 (.clk(clock_1_out), .Qn(S1_qn));  // open: D, Q, preset, en, reset
  D_Flip_Flop S1_2 (.clk(clock_1_out), .Qn(S1_2_qn));  // open: D, Q, preset, en, reset
endmodule
